# Fritzing sketch Mini Hydrophonics Schematic (saved by Fritzing 1.0.6)

parts:
  Relays = 6 channel relay module
  Arduino_Mega = Arduino Mega 2560 (Rev3)
  24V_-_5V = LM2596 step down module
  J3 = Camdenboss CTB0158-2 [part_number=CTB0158-2 package=THT]
  J4 = Camdenboss CTB0158-2 [part_number=CTB0158-2 package=THT]
  J5 = Camdenboss CTB0158-2 [part_number=CTB0158-2 package=THT]
  J6 = Camdenboss CTB0158-2 [part_number=CTB0158-2 package=THT]
  J7 = Camdenboss CTB0158-2 [part_number=CTB0158-2 package=THT]
  J8 = Camdenboss CTB0158-2 [part_number=CTB0158-2 package=THT]
  Grow_Light = 60mm 8x8 dot matrix column cathode led display with standard pcb pads
  WReservoir_WPump = water pump/motor
  Mixer = DC Motor [voltage_(max)=6V voltage_(min)=3V]
  PUMP_-_GC = water pump/motor
  M1 = PH meter with sensor in breadboard [package=THT]
  Water_Level_Sensor = HC-SR04 Ultrasonic Distance Sensor
  A1 = tds-sensor-meter-v1.0_1
  J14 = Wago 221-413
  +24_V_Splicer = Wago 221-413
  J15 = Wago 221-413
  BAT1 = 24 battery [package=battery]
  -24_V_Splicer = Wago 221-413
  PH_WPump_[stepper] = Stepper Motor - Bipolar
  Nutrient_Mix_WPump_[stepper] = Stepper Motor - Bipolar
  J16 = Wago 221-413
  24V_-_12V = LM2596 step down module
  J17 = Wago 221-413
  J18 = Wago 221-413
  Adafruit_A4988_Stepper_Motor_Driver_Breakout1 = Adafruit A4988 Stepper Motor Driver Breakout [mn=Adafruit mpn=#6109 part_number=#6109]
  Adafruit_A4988_Stepper_Motor_Driver_Breakout2 = Adafruit A4988 Stepper Motor Driver Breakout [mn=Adafruit mpn=#6109 part_number=#6109]

nets:
  N1: Relays.Pin_2, Arduino_Mega.D13_PWM
  N2: Relays.Pin_3, Arduino_Mega.D12_PWM
  N3: Relays.Pin_4, Arduino_Mega.D11_PWM
  N4: Relays.Pin_5, Arduino_Mega.D10_PWM
  N5: Relays.Pin_6, Arduino_Mega.D9_PWM
  N6: Relays.Pin_7, Arduino_Mega.D8_PWM
  GND: Relays.Pin_12, Arduino_Mega.GND, 24V_-_5V.IN-, 24V_-_5V.OUT-, M1.pin3, Water_Level_Sensor.GND, A1.pin3, J14.Pin_1, J14.Pin_2, J14.Pin_3, BAT1.-, -24_V_Splicer.Pin_1, -24_V_Splicer.Pin_2, -24_V_Splicer.Pin_3, 24V_-_12V.IN+, 24V_-_12V.OUT+, J17.Pin_1, J17.Pin_2, J17.Pin_3, J18.Pin_1, J18.Pin_2, J18.Pin_3
  N7: Relays.Pin_13, J3.pin1
  N8: Relays.Pin_16, J4.pin1
  N9: Relays.Pin_19, J5.pin1
  N10: Relays.Pin_22, J6.pin1
  N11: Relays.Pin_25, J7.pin1
  N12: Relays.Pin_28, J8.pin1
  N13: Arduino_Mega.A0, M1.pin1
  N14: Arduino_Mega.A1, A1.pin1
  5V: Arduino_Mega.5V, 24V_-_5V.OUT+, M1.pin2, Water_Level_Sensor.VCC, A1.pin2, J15.Pin_1, J15.Pin_2, J15.Pin_3
  N15: Arduino_Mega.D2_PWM, Adafruit_A4988_Stepper_Motor_Driver_Breakout2.STEP
  N16: Arduino_Mega.D3_PWM, Adafruit_A4988_Stepper_Motor_Driver_Breakout2.DIR
  N17: Arduino_Mega.D6_PWM, Adafruit_A4988_Stepper_Motor_Driver_Breakout1.STEP
  N18: Arduino_Mega.D7_PWM, Adafruit_A4988_Stepper_Motor_Driver_Breakout1.DIR
  N19: Arduino_Mega.D41, Water_Level_Sensor.TRIG
  N20: Arduino_Mega.D43, Water_Level_Sensor.ECHO
  N21: 24V_-_5V.IN+, J3.pin2, J8.pin2, +24_V_Splicer.Pin_1, +24_V_Splicer.Pin_2, +24_V_Splicer.Pin_3, BAT1.+, J16.Pin_1, J16.Pin_2, J16.Pin_3, 24V_-_12V.IN-, 24V_-_12V.OUT-
  N22: J3.terminal_1, Grow_Light.pin_1
  N23: J3.terminal_2, Grow_Light.pin_2
  N24: J4.terminal_1, Adafruit_A4988_Stepper_Motor_Driver_Breakout1.VDD
  N25: J4.terminal_2, Adafruit_A4988_Stepper_Motor_Driver_Breakout1.GND
  N26: J5.terminal_1, Adafruit_A4988_Stepper_Motor_Driver_Breakout2.VDD
  N27: J5.terminal_2, Adafruit_A4988_Stepper_Motor_Driver_Breakout2.GND
  N28: J6.terminal_1, WReservoir_WPump.pin_2
  N29: J6.terminal_2, WReservoir_WPump.pin_1
  N30: J7.terminal_1, Mixer.pin_1
  N31: J7.terminal_2, Mixer.pin_2
  N32: J8.terminal_1, PUMP_-_GC.pin_2
  N33: J8.terminal_2, PUMP_-_GC.pin_1
  N34: PH_WPump_[stepper].A, Adafruit_A4988_Stepper_Motor_Driver_Breakout1.OUT2B
  N35: PH_WPump_[stepper].C, Adafruit_A4988_Stepper_Motor_Driver_Breakout1.OUT2A
  N36: PH_WPump_[stepper].B, Adafruit_A4988_Stepper_Motor_Driver_Breakout1.OUT1A
  N37: PH_WPump_[stepper].D, Adafruit_A4988_Stepper_Motor_Driver_Breakout1.OUT1B
  N38: Nutrient_Mix_WPump_[stepper].A, Adafruit_A4988_Stepper_Motor_Driver_Breakout2.OUT2B
  N39: Nutrient_Mix_WPump_[stepper].C, Adafruit_A4988_Stepper_Motor_Driver_Breakout2.OUT2A
  N40: Nutrient_Mix_WPump_[stepper].B, Adafruit_A4988_Stepper_Motor_Driver_Breakout2.OUT1A
  N41: Nutrient_Mix_WPump_[stepper].D, Adafruit_A4988_Stepper_Motor_Driver_Breakout2.OUT1B

custom parts:
  6 channel relay module: 6 Channel 5V Relay Board Module Optocoupler LED.
  LM2596 step down module: LM2596 DC-DC step down power supply module 3 A.
  water pump/motor: WATER PUMP BY ARDUBLOCKTR
  PH meter with sensor in breadboard: DFrobot PH meter (SKU SEN0161)
  : TDS Meter V1.0 Development Board Water Meter Filter Measuring Water Sensor Module.
  Wago 221-413: Wago 221-413 3 position splicing connector 12AWG.
  24 battery: 24V lead acid type battery, like the Husqvarna YTH2448 12V 35AH battery. This is the mini version 1/4 the size of the actual battery to be closer to typical breadboard parts (around 2in wide rathher than 7in). The pads in pcb are sized to accomidate up to 14ga wire (as these batterys will deliver high currents.)
